# Fritzing sketch terratech (saved by Fritzing 0.9.3b)
breadboards: 1

parts:
  Raspberry_Pi_1 = Raspberry Pi 3 [part_number=RPI-3-V1.2]
  LED1 = LED - 5mm [color="Red (633nm)" package="5 mm [THT]"]
  LED2 = LED - 5mm [color="Green (560nm)" package="5 mm [THT]"]
  R1 = Resistor [tolerance=±5% resistance=220 package=THT]
  Soil_Sensor_Probe = FC-28 Soil Hygrometer Module - Probe
  Soil_Sensor = FC-28 Soil Hygrometer Module
  Relay = KY-019 5V Relay Module [package="Breakout board"]
  Water_Pump = water pump/motor
  DHT11 = Humidity and Temperature Sensor DHT11
  R3 = Resistor [tolerance=±5% resistance=10k package=THT]
  R2 = Resistor [tolerance=±5% resistance=220 package=THT]

nets (from the schematic view):
  3V3: Raspberry_Pi_1.3v3, Raspberry_Pi_1.3V3, Relay.+
  N1: Raspberry_Pi_1.GPIO4, LED2.cathode
  N2: Raspberry_Pi_1.GPIO17, LED1.cathode
  N3: Raspberry_Pi_1.GPIO27, Relay.S
  GND: Raspberry_Pi_1.GND, R1.Pin_1, Soil_Sensor.GND, Relay.-, Water_Pump.pin_2, DHT11.GND_2, R2.Pin_1
  N4: Raspberry_Pi_1.GPIO21, Soil_Sensor.DO
  N5: Raspberry_Pi_1.GPIO23, DHT11.Data-signal
  VCC: Raspberry_Pi_1.5V, Soil_Sensor.VCC, Relay.Common, DHT11.Vcc, R3.Pin_0
  N6: LED1.anode, R1.Pin_0
  N7: LED2.anode, R2.Pin_0
  N8: Soil_Sensor_Probe.POS, Soil_Sensor.POS
  N9: Soil_Sensor_Probe.NEG, Soil_Sensor.NEG
  N10: Relay.NO, Water_Pump.pin_1

custom parts:
  FC-28 Soil Hygrometer Module - Probe: The FC-28 is a soil hygrometer module that uses the Texas Instruments LM393 comparator chip to provide an analog measurement of soil humidity.
  FC-28 Soil Hygrometer Module: The FC-28 is a soil hygrometer module that uses the Texas Instruments LM393 comparator chip to provide an analog measurement of soil humidity. The digital output is high when soil moisture is over a certain threshold, as determined by adjusting the potentiometer.
  KY-019 5V Relay Module: KY-019 5V Relay module, used to control AC circuits. (Special thanks to vanepp for fixing the PCB holes and other errors)
  water pump/motor: WATER PUMP BY ARDUBLOCKTR
  Humidity and Temperature Sensor DHT11: Digital relative humidity & temperature sensor DHT11
